// Logisim project Codificadores-Decodificadores.circ as structural Verilog
module COD_4x2 (
  input  A3,
  input  A2,
  input  A1,
  input  A0,
  output D1,
  output D0
);

  or or_1 (D1, A2, A3);
  or or_2 (D0, A1, A3);
endmodule

module DECOD_2x4 (
  input  D1,
  input  D0,
  output Y3,
  output Y2,
  output Y1,
  output Y0
);

  wire not_1_out, not_2_out, not_3_out, not_4_out;

  and and_1 (Y3, D1, D0);
  and and_2 (Y2, D1, not_1_out);
  not not_1 (not_1_out, D0);
  not not_2 (not_2_out, D1);
  and and_3 (Y1, not_2_out, D0);
  not not_3 (not_3_out, D1);
  and and_4 (Y0, not_3_out, not_4_out);
  not not_4 (not_4_out, D0);
endmodule
