// Logisim project Latches-FlipFlops.circ as structural Verilog: 24 circuits, main circuit main
module main (
  input  in_1,
  input  in_2,
  input  in_3,
  input  in_4,
  input  in_5,
  input  in_6,
  input  in_7,
  input  in_8,
  input  in_9,
  input  in_10,
  output out_11,
  output out_12,
  output out_13,
  output out_14,
  output out_15,
  output out_16,
  output out_17,
  output out_18,
  output out_19,
  output out_20,
  output out_21
);

  wire clock_1_out, controle_de_borda_1_out_2, not_1_out;

  Clock clock_1 (.out(clock_1_out));
  Controle_de_Borda controle_de_borda_1 (.in_1(clock_1_out), .out_2(controle_de_borda_1_out_2));
  not not_1 (not_1_out, controle_de_borda_1_out_2);
  \Contador_Síncrono_Módulo_16__EN_OUT__CLK__EN_CLK__LOAD__CLR  \contador_síncrono_módulo_16_en_out_clk_en_clk_load_clr_1  (
    .EN_OUT(in_1), .EN_CLK(in_2), .LOAD(in_3), .CLR(in_4), .Q0(out_14), .Q1(out_13), .Q2(out_12),
    .Q3(out_11), .D0(in_8), .D1(in_7), .D2(in_6), .D3(in_5), .CLK(controle_de_borda_1_out_2));
  \Contador_Assíncrono_Módulo_16__CLK__CLR  \contador_assíncrono_módulo_16_clk_clr_1  (
    .CLK(not_1_out), .CLR(in_10), .Q3(out_18), .Q2(out_19), .Q1(out_20), .Q0(out_21));
  \Contador_Síncrono_Módulo_8__Sequência_Personalizada  \contador_síncrono_módulo_8_sequência_personalizada_1  (
    .CLK(controle_de_borda_1_out_2), .\Início (in_9), .Q0(out_17), .Q1(out_16), .Q3(out_15));
endmodule

module Latch_SR__NOR (
  input  S,
  input  R,
  output \Não_Q ,
  output Q
);

  nor nor_1 (\Não_Q , S, Q);
  nor nor_2 (Q, \Não_Q , R);
endmodule

module Latch_SR__NAND (
  input  S,
  input  R,
  output \Não_Q ,
  output Q
);

  nand nand_1 (\Não_Q , S, Q);
  nand nand_2 (Q, \Não_Q , R);
endmodule

module Latch_SR_Controlado__NAND (
  input  S,
  input  EN,
  input  R,
  output Q,
  output \Não_Q 
);

  wire nand_1_out, nand_2_out;

  nand nand_1 (nand_1_out, S, EN);
  nand nand_2 (nand_2_out, EN, R);
  nand nand_3 (Q, nand_1_out, \Não_Q );
  nand nand_4 (\Não_Q , Q, nand_2_out);
endmodule

module Latch_em_D__NAND (
  input  S,
  input  EN,
  output Q,
  output \Não_Q 
);

  wire nand_1_out, nand_2_out, not_1_out;

  not not_1 (not_1_out, S);
  nand nand_1 (nand_1_out, S, EN);
  nand nand_2 (nand_2_out, EN, not_1_out);
  nand nand_3 (Q, nand_1_out, \Não_Q );
  nand nand_4 (\Não_Q , Q, nand_2_out);
endmodule

module Flip_Flop_SR__NAND (
  input  Preset,
  input  S,
  input  CLK,
  input  R,
  input  Clear,
  output Q,
  output nQ
);

  wire controle_de_borda_1_out_2, nand_1_out, nand_2_out, not_1_out, not_2_out;

  Controle_de_Borda controle_de_borda_1 (.in_1(CLK), .out_2(controle_de_borda_1_out_2));
  nand nand_1 (nand_1_out, S, controle_de_borda_1_out_2);
  nand nand_2 (nand_2_out, controle_de_borda_1_out_2, R);
  not not_1 (not_1_out, Preset);
  not not_2 (not_2_out, Clear);
  nand nand_3 (Q, not_1_out, nand_1_out, nQ);
  nand nand_4 (nQ, Q, nand_2_out, not_2_out);
endmodule

module Flip_Flop_JK__PRE_CLR (
  input  Preset,
  input  J,
  input  CLK,
  input  K,
  input  Clear,
  output Q,
  output nQ
);

  wire and_1_out, and_2_out, controle_de_borda_1_out_2, nand_1_out, nand_2_out, not_1_out, not_2_out;

  and and_1 (and_1_out, nQ, J);
  Controle_de_Borda controle_de_borda_1 (.in_1(CLK), .out_2(controle_de_borda_1_out_2));
  and and_2 (and_2_out, K, Q);
  not not_1 (not_1_out, Preset);
  nand nand_1 (nand_1_out, and_1_out, controle_de_borda_1_out_2);
  nand nand_2 (nand_2_out, controle_de_borda_1_out_2, and_2_out);
  not not_2 (not_2_out, Clear);
  nand nand_3 (Q, not_1_out, nand_1_out, nQ);
  nand nand_4 (nQ, Q, nand_2_out, not_2_out);
endmodule

module Flip_Flop_T__PRE__CLR (
  input  PRE,
  input  T,
  input  CLK,
  input  CLR,
  output Q,
  output nQ
);

  wire controle_de_borda_1_out_2;

  Controle_de_Borda controle_de_borda_1 (.in_1(CLK), .out_2(controle_de_borda_1_out_2));
  Flip_Flop_JK__PRE_CLR ff_jk_pre_clr_1 (
    .J(T), .Q(Q), .nQ(nQ), .K(T), .Preset(PRE), .Clear(CLR), .CLK(controle_de_borda_1_out_2));
endmodule

module Flip_Flop_D__PRE_CLR (
  input  PRE,
  input  D,
  input  CLK,
  input  CLR,
  output Q,
  output nQ
);

  wire controle_de_borda_1_out_2, nand_1_out, nand_2_out, not_1_out, not_2_out;

  Controle_de_Borda controle_de_borda_1 (.in_1(CLK), .out_2(controle_de_borda_1_out_2));
  not not_1 (not_1_out, PRE);
  nand nand_1 (nand_1_out, D, controle_de_borda_1_out_2);
  nand nand_2 (nand_2_out, controle_de_borda_1_out_2, ~D);  // NAND_Gate
  not not_2 (not_2_out, CLR);
  nand nand_3 (Q, not_1_out, nand_1_out, nQ);
  nand nand_4 (nQ, Q, nand_2_out, not_2_out);
endmodule

module Controle_de_Borda (
  input  in_1,
  output out_2
);

  wire and_1_out, not_1_out;

  not not_1 (not_1_out, in_1);
  and and_1 (and_1_out, not_1_out, not_1_out);
  and and_2 (out_2, in_1, and_1_out);
endmodule

module \Contador_Assíncrono_Módulo_16__CLK__CLR  (
  input  CLK,
  input  CLR,
  output Q3,
  output Q2,
  output Q1,
  output Q0
);

  wire controle_de_borda_1_out_2, not_1_out, not_2_out, not_3_out, not_4_out;

  Controle_de_Borda controle_de_borda_1 (.in_1(CLK), .out_2(controle_de_borda_1_out_2));
  not not_1 (not_1_out, controle_de_borda_1_out_2);
  Flip_Flop_T__PRE__CLR ff_t_pre_clr_1 (.T(1'b1), .Q(Q0), .PRE(1'b0), .CLR(CLR), .CLK(not_1_out));  // open: nQ
  Flip_Flop_T__PRE__CLR ff_t_pre_clr_2 (.T(1'b1), .Q(Q1), .PRE(1'b0), .CLR(CLR), .CLK(not_2_out));  // open: nQ
  not not_2 (not_2_out, Q0);
  not not_3 (not_3_out, Q1);
  Flip_Flop_T__PRE__CLR ff_t_pre_clr_3 (.T(1'b1), .Q(Q2), .PRE(1'b0), .CLR(CLR), .CLK(not_3_out));  // open: nQ
  not not_4 (not_4_out, Q2);
  Flip_Flop_T__PRE__CLR ff_t_pre_clr_4 (.T(1'b1), .Q(Q3), .PRE(1'b0), .CLR(CLR), .CLK(not_4_out));  // open: nQ

  // Notes on the sheet:
  //   INÍCIO
endmodule

module \Contador_Síncrono_Módulo_16__EN_OUT__CLK__EN_CLK__LOAD__CLR  (
  input  EN_OUT,
  input  CLK,
  input  EN_CLK,
  input  LOAD,
  input  CLR,
  input  D0,
  input  D1,
  input  D2,
  input  D3,
  output Q0,
  output Q1,
  output Q2,
  output Q3
);

  wire and_1_out, and_2_out, and_3_out, and_4_out, and_5_out, and_6_out, and_7_out, and_8_out, and_9_out,
       and_10_out, ff_t_pre_clr_spre_sclr_clk_en_1_q, ff_t_pre_clr_spre_sclr_clk_en_2_q,
       ff_t_pre_clr_spre_sclr_clk_en_3_q, ff_t_pre_clr_spre_sclr_clk_en_4_q;

  and and_1 (and_1_out, D0, LOAD);
  and and_2 (and_2_out, ~D0, LOAD);  // AND_Gate
  assign Q0 = EN_OUT ? ff_t_pre_clr_spre_sclr_clk_en_1_q : 1'bz;  // Controlled_Buffer controlled_buffer_1
  Flip_Flop_T__PRE__CLR__sPRE__sCLR__CLK_EN ff_t_pre_clr_spre_sclr_clk_en_1 (
    .T(1'b1), .CLK(CLK), .Q(ff_t_pre_clr_spre_sclr_clk_en_1_q), .sPRE(and_1_out), .PRE(1'b0),
    .sCLR(and_2_out), .EN(EN_CLK), .CLR(CLR));  // open: nQ
  and and_3 (and_3_out, D1, LOAD);
  and and_4 (and_4_out, ~D1, LOAD);  // AND_Gate
  assign Q1 = EN_OUT ? ff_t_pre_clr_spre_sclr_clk_en_2_q : 1'bz;  // Controlled_Buffer controlled_buffer_2
  Flip_Flop_T__PRE__CLR__sPRE__sCLR__CLK_EN ff_t_pre_clr_spre_sclr_clk_en_2 (
    .T(ff_t_pre_clr_spre_sclr_clk_en_1_q), .CLK(CLK), .Q(ff_t_pre_clr_spre_sclr_clk_en_2_q),
    .sPRE(and_3_out), .PRE(1'b0), .sCLR(and_4_out), .EN(EN_CLK), .CLR(CLR));  // open: nQ
  and and_5 (and_5_out, ff_t_pre_clr_spre_sclr_clk_en_1_q, ff_t_pre_clr_spre_sclr_clk_en_2_q);
  assign Q2 = EN_OUT ? ff_t_pre_clr_spre_sclr_clk_en_3_q : 1'bz;  // Controlled_Buffer controlled_buffer_3
  and and_6 (and_6_out, D2, LOAD);
  Flip_Flop_T__PRE__CLR__sPRE__sCLR__CLK_EN ff_t_pre_clr_spre_sclr_clk_en_3 (
    .T(and_5_out), .CLK(CLK), .Q(ff_t_pre_clr_spre_sclr_clk_en_3_q), .sPRE(and_6_out), .PRE(1'b0),
    .sCLR(and_7_out), .EN(EN_CLK), .CLR(CLR));  // open: nQ
  and and_7 (and_7_out, ~D2, LOAD);  // AND_Gate
  and and_8 (and_8_out, and_5_out, ff_t_pre_clr_spre_sclr_clk_en_3_q);
  and and_9 (and_9_out, D3, LOAD);
  and and_10 (and_10_out, ~D3, LOAD);  // AND_Gate
  assign Q3 = EN_OUT ? ff_t_pre_clr_spre_sclr_clk_en_4_q : 1'bz;  // Controlled_Buffer controlled_buffer_4
  Flip_Flop_T__PRE__CLR__sPRE__sCLR__CLK_EN ff_t_pre_clr_spre_sclr_clk_en_4 (
    .T(and_8_out), .CLK(CLK), .Q(ff_t_pre_clr_spre_sclr_clk_en_4_q), .sPRE(and_9_out), .PRE(1'b0),
    .sCLR(and_10_out), .EN(EN_CLK), .CLR(CLR));  // open: nQ
endmodule

module Flip_Flop_JK__PRE__CLR__sPRE__sCLR__CLK_EN (
  input  PRE,
  input  J,
  input  CLK,
  input  K,
  input  CLR,
  input  sPRE,
  input  sCLR,
  input  CLK_EN,
  output Q,
  output nQ
);

  wire and_1_out, and_2_out, and_3_out, and_4_out, or_1_out, or_2_out;

  or or_1 (or_1_out, J, sPRE);
  and and_1 (and_1_out, ~sPRE, K);  // AND_Gate
  and and_2 (and_2_out, or_1_out, ~sCLR);  // AND_Gate
  or or_2 (or_2_out, sCLR, and_1_out);
  and and_3 (and_3_out, and_2_out, CLK_EN);
  and and_4 (and_4_out, CLK_EN, or_2_out);
  Flip_Flop_JK__PRE_CLR ff_jk_pre_clr_1 (
    .J(and_3_out), .Q(Q), .nQ(nQ), .K(and_4_out), .Preset(PRE), .Clear(CLR), .CLK(CLK));
endmodule

module Flip_Flop_T__PRE__CLR__sPRE__sCLR__CLK_EN (
  input  sPRE,
  input  PRE,
  input  T,
  input  CLK,
  input  sCLR,
  input  EN,
  input  CLR,
  output Q,
  output nQ
);

  Flip_Flop_JK__PRE__CLR__sPRE__sCLR__CLK_EN ff_jk_pre_clr_spre_sclr_clk_en_1 (
    .J(T), .K(T), .Q(Q), .nQ(nQ), .PRE(PRE), .sPRE(sPRE), .sCLR(sCLR), .CLK_EN(EN), .CLR(CLR), .CLK(CLK));
endmodule

module Registrador_4_bits__EN_OUT__LOAD (
  input  EN_OUT,
  input  LOAD,
  input  I3,
  input  I2,
  input  I1,
  input  I0,
  output O3,
  output O2,
  output O1,
  output O0
);

  wire latch_em_d_nand_1_q, latch_em_d_nand_2_q, latch_em_d_nand_3_q, latch_em_d_nand_4_q;

  Latch_em_D__NAND latch_em_d_nand_1 (.S(I3), .EN(LOAD), .Q(latch_em_d_nand_1_q));  // open: Não_Q
  assign O3 = EN_OUT ? latch_em_d_nand_1_q : 1'bz;  // Controlled_Buffer controlled_buffer_1
  assign O2 = EN_OUT ? latch_em_d_nand_2_q : 1'bz;  // Controlled_Buffer controlled_buffer_2
  Latch_em_D__NAND latch_em_d_nand_2 (.S(I2), .EN(LOAD), .Q(latch_em_d_nand_2_q));  // open: Não_Q
  assign O1 = EN_OUT ? latch_em_d_nand_3_q : 1'bz;  // Controlled_Buffer controlled_buffer_3
  Latch_em_D__NAND latch_em_d_nand_3 (.S(I1), .EN(LOAD), .Q(latch_em_d_nand_3_q));  // open: Não_Q
  assign O0 = EN_OUT ? latch_em_d_nand_4_q : 1'bz;  // Controlled_Buffer controlled_buffer_4
  Latch_em_D__NAND latch_em_d_nand_4 (.S(I0), .EN(LOAD), .Q(latch_em_d_nand_4_q));  // open: Não_Q
endmodule

module Registrador_8_bits__EN_OUT__LOAD (
  input  EN_OUT,
  input  LOAD,
  input  I7,
  input  I6,
  input  I5,
  input  I4,
  input  I3,
  input  I2,
  input  I1,
  input  I0,
  output O7,
  output O6,
  output O5,
  output O4,
  output O3,
  output O2,
  output O1,
  output O0
);

  Registrador_4_bits__EN_OUT__LOAD registrador_4_bits_en_out_load_1 (
    .EN_OUT(EN_OUT), .LOAD(LOAD), .O3(O7), .O2(O6), .O1(O5), .O0(O4), .I3(I7), .I2(I6), .I1(I5), .I0(I4));
  Registrador_4_bits__EN_OUT__LOAD registrador_4_bits_en_out_load_2 (
    .EN_OUT(EN_OUT), .LOAD(LOAD), .O3(O3), .O2(O2), .O1(O1), .O0(O0), .I3(I3), .I2(I2), .I1(I1), .I0(I0));
endmodule

module \Contador_Síncrono_Módulo_8__Sequência_Personalizada  (
  input  CLK,
  input  \Início ,
  output Q0,
  output Q1,
  output Q3
);

  wire and_1_out, and_2_out, controle_de_borda_1_out_2, or_1_out;

  Controle_de_Borda controle_de_borda_1 (.in_1(CLK), .out_2(controle_de_borda_1_out_2));
  Flip_Flop_T__PRE__CLR ff_t_pre_clr_1 (
    .T(1'b1), .Q(Q0), .PRE(or_1_out), .CLR(1'b0), .CLK(controle_de_borda_1_out_2));  // open: nQ
  Flip_Flop_T__PRE__CLR ff_t_pre_clr_2 (
    .T(Q0), .Q(Q1), .PRE(1'b0), .CLR(or_1_out), .CLK(controle_de_borda_1_out_2));  // open: nQ
  or or_1 (or_1_out, \Início , and_2_out);
  and and_1 (and_1_out, Q0, Q1);
  Flip_Flop_T__PRE__CLR ff_t_pre_clr_3 (
    .T(and_1_out), .Q(Q3), .PRE(1'b0), .CLR(or_1_out), .CLK(controle_de_borda_1_out_2));  // open: nQ
  and and_2 (and_2_out, Q3, Q1, ~Q0);  // AND_Gate
endmodule

module Contador_em_Anel (
  input  CLK,
  input  START,
  output Q0,
  output Q1,
  output Q2,
  output Q3,
  output Q4,
  output Q5
);

  wire controle_de_borda_1_out_2;

  Controle_de_Borda controle_de_borda_1 (.in_1(CLK), .out_2(controle_de_borda_1_out_2));
  Flip_Flop_D__PRE_CLR ff_d_pre_clr_1 (
    .D(Q5), .Q(Q0), .PRE(START), .CLR(1'b0), .CLK(controle_de_borda_1_out_2));  // open: nQ
  Flip_Flop_D__PRE_CLR ff_d_pre_clr_2 (
    .D(Q0), .Q(Q1), .PRE(1'b0), .CLR(START), .CLK(controle_de_borda_1_out_2));  // open: nQ
  Flip_Flop_D__PRE_CLR ff_d_pre_clr_3 (
    .D(Q1), .Q(Q2), .PRE(1'b0), .CLR(START), .CLK(controle_de_borda_1_out_2));  // open: nQ
  Flip_Flop_D__PRE_CLR ff_d_pre_clr_4 (
    .D(Q2), .Q(Q3), .PRE(1'b0), .CLR(START), .CLK(controle_de_borda_1_out_2));  // open: nQ
  Flip_Flop_D__PRE_CLR ff_d_pre_clr_5 (
    .D(Q3), .Q(Q4), .PRE(1'b0), .CLR(START), .CLK(controle_de_borda_1_out_2));  // open: nQ
  Flip_Flop_D__PRE_CLR ff_d_pre_clr_6 (
    .D(Q4), .Q(Q5), .PRE(1'b0), .CLR(START), .CLK(controle_de_borda_1_out_2));  // open: nQ
endmodule

module \Máquina_de_Estados_Finitos_1  (
  input  CLK,
  input  CLR,
  output Y3,
  output Y2,
  output Y1,
  output Y0
);

  wire \contador_síncrono_módulo_4_1_q0 , \contador_síncrono_módulo_4_1_q1 , controle_de_borda_1_out_2;

  Controle_de_Borda controle_de_borda_1 (.in_1(CLK), .out_2(controle_de_borda_1_out_2));
  nor nor_1 (Y3, \contador_síncrono_módulo_4_1_q1 , \contador_síncrono_módulo_4_1_q0 );
  \Contador_Síncrono_Módulo_4  \contador_síncrono_módulo_4_1  (
    .CLK(controle_de_borda_1_out_2), .\Início (CLR), .Q0(\contador_síncrono_módulo_4_1_q0 ),
    .Q1(\contador_síncrono_módulo_4_1_q1 ));
  not not_1 (Y2, Y3);
  not not_2 (Y1, \contador_síncrono_módulo_4_1_q0 );
  xor xor_1 (Y0, \contador_síncrono_módulo_4_1_q1 , \contador_síncrono_módulo_4_1_q0 );
endmodule

module \Contador_Síncrono_Módulo_4  (
  input  CLK,
  input  \Início ,
  output Q0,
  output Q1
);

  wire controle_de_borda_1_out_2;

  Controle_de_Borda controle_de_borda_1 (.in_1(CLK), .out_2(controle_de_borda_1_out_2));
  Flip_Flop_T__PRE__CLR ff_t_pre_clr_1 (
    .T(1'b1), .Q(Q0), .PRE(1'b0), .CLR(\Início ), .CLK(controle_de_borda_1_out_2));  // open: nQ
  Flip_Flop_T__PRE__CLR ff_t_pre_clr_2 (
    .T(Q0), .Q(Q1), .PRE(1'b0), .CLR(\Início ), .CLK(controle_de_borda_1_out_2));  // open: nQ
endmodule

module \Máquina_de_Estados_Finitos_2__Q10  (
  input  A,
  input  CLK,
  input  CLR,
  output Y3,
  output Y2,
  output Y1,
  output Y0
);

  wire controle_de_borda_1_out_2, \lógica_de_transição_de_estados_q10_1_q0_2 ,
       \lógica_de_transição_de_estados_q10_1_q1_2 , registrador_2_bits_1_q0_plus,
       registrador_2_bits_1_q1_plus;

  Controle_de_Borda controle_de_borda_1 (.in_1(CLK), .out_2(controle_de_borda_1_out_2));
  \Lógica_de_Transição_de_Estados__Q10  \lógica_de_transição_de_estados_q10_1  (
    .Q1_2(\lógica_de_transição_de_estados_q10_1_q1_2 ), .Q0_2(\lógica_de_transição_de_estados_q10_1_q0_2 ),
    .A(A), .Q1(registrador_2_bits_1_q1_plus), .Q0(registrador_2_bits_1_q0_plus));
  Registrador_2_bits registrador_2_bits_1 (
    .CLK(controle_de_borda_1_out_2), .CLR(CLR), .Q1_plus(registrador_2_bits_1_q1_plus),
    .Q0_plus(registrador_2_bits_1_q0_plus), .Q1(\lógica_de_transição_de_estados_q10_1_q1_2 ),
    .Q0(\lógica_de_transição_de_estados_q10_1_q0_2 ));
  \Lógica_de_Saída__Q10  \lógica_de_saída_q10_1  (
    .Y3(Y3), .Y2(Y2), .Y1(Y1), .Y0(Y0), .Q1(registrador_2_bits_1_q1_plus), .Q0(registrador_2_bits_1_q0_plus));
endmodule

module Registrador_2_bits (
  input  CLK,
  input  CLR,
  input  Q1,
  input  Q0,
  output Q1_plus,
  output Q0_plus
);

  wire controle_de_borda_1_out_2;

  Controle_de_Borda controle_de_borda_1 (.in_1(CLK), .out_2(controle_de_borda_1_out_2));
  Flip_Flop_D__PRE_CLR ff_d_pre_clr_1 (
    .D(Q1), .Q(Q1_plus), .PRE(1'b0), .CLR(CLR), .CLK(controle_de_borda_1_out_2));  // open: nQ
  Flip_Flop_D__PRE_CLR ff_d_pre_clr_2 (
    .D(Q0), .Q(Q0_plus), .PRE(1'b0), .CLR(CLR), .CLK(controle_de_borda_1_out_2));  // open: nQ
endmodule

module \Lógica_de_Transição_de_Estados__Q10  (
  input  A,
  input  Q1,
  input  Q0,
  output Q1_2,
  output Q0_2
);

  wire and_1_out, and_2_out, and_3_out, and_4_out, and_5_out;

  and and_1 (and_1_out, ~A, Q1, Q0);  // AND_Gate
  and and_2 (and_2_out, A, ~Q1, Q0);  // AND_Gate
  and and_3 (and_3_out, A, Q1, ~Q0);  // AND_Gate
  and and_4 (and_4_out, ~A, Q0);  // AND_Gate
  and and_5 (and_5_out, A, ~Q0);  // AND_Gate
  or or_1 (Q1_2, and_1_out, and_2_out, and_3_out);
  or or_2 (Q0_2, and_4_out, and_5_out);
endmodule

module \Lógica_de_Saída__Q10  (
  input  Q1,
  input  Q0,
  output Y3,
  output Y2,
  output Y1,
  output Y0
);

  or or_1 (Y3, Q1, Q0);
  not not_1 (Y2, Q0);
  and and_1 (Y1, Q0, Q1);
  not not_2 (Y0, Q1);
endmodule
