// Logisim project Lista2.circ as structural Verilog
module Q01 (
  input  PRE,
  input  D,
  input  CLR,
  output Q,
  output nQ
);

  wire clock_1_out, controle_de_borda_1_out_2, xor_1_out;

  Clock clock_1 (.out(clock_1_out));
  Controle_de_Borda controle_de_borda_1 (.in_1(clock_1_out), .out_2(controle_de_borda_1_out_2));
  xor xor_1 (xor_1_out, Q, D);
  Flip_Flop_T__PRE__CLR ff_t_pre_clr_1 (
    .T(xor_1_out), .Q(Q), .nQ(nQ), .PRE(PRE), .CLR(CLR), .CLK(controle_de_borda_1_out_2));
endmodule

module Q02 (
  input  PRE,
  input  T,
  input  CLR,
  output Q,
  output nQ
);

  wire clock_1_out, controle_de_borda_1_out_2, xor_1_out;

  Clock clock_1 (.out(clock_1_out));
  Controle_de_Borda controle_de_borda_1 (.in_1(clock_1_out), .out_2(controle_de_borda_1_out_2));
  xor xor_1 (xor_1_out, Q, T);
  Flip_Flop_D__PRE_CLR ff_d_pre_clr_1 (
    .D(xor_1_out), .Q(Q), .nQ(nQ), .PRE(PRE), .CLR(CLR), .CLK(controle_de_borda_1_out_2));
endmodule

module Q03 (
  input  PRE,
  input  J,
  input  K,
  input  CLR,
  output Q,
  output nQ
);

  wire and_1_out, and_2_out, clock_1_out, controle_de_borda_1_out_2;

  Clock clock_1 (.out(clock_1_out));
  and and_1 (and_1_out, nQ, J);
  Controle_de_Borda controle_de_borda_1 (.in_1(clock_1_out), .out_2(controle_de_borda_1_out_2));
  and and_2 (and_2_out, K, Q);
  Flip_Flop_SR__NAND ff_sr_nand_1 (
    .Preset(PRE), .S(and_1_out), .Q(Q), .R(and_2_out), .Clear(CLR), .CLK(controle_de_borda_1_out_2), .nQ(nQ));
endmodule

module Q04 (
  input  in_1,
  output out_2,
  output out_3,
  output out_4,
  output out_5
);

  wire clock_1_out, controle_de_borda_1_out_2, not_1_out;

  Clock clock_1 (.out(clock_1_out));
  Controle_de_Borda controle_de_borda_1 (.in_1(clock_1_out), .out_2(controle_de_borda_1_out_2));
  not not_1 (not_1_out, controle_de_borda_1_out_2);
  \Contador_Assíncrono_Módulo_16__CLK__CLR  \contador_assíncrono_módulo_16_clk_clr_1  (
    .CLK(not_1_out), .CLR(in_1), .Q3(out_2), .Q2(out_3), .Q1(out_4), .Q0(out_5));
endmodule

module Q05 (
  input  in_1,
  input  in_2,
  input  in_3,
  input  in_4,
  input  in_5,
  input  in_6,
  input  in_7,
  input  in_8,
  output out_9,
  output out_10,
  output out_11,
  output out_12
);

  wire clock_1_out, controle_de_borda_1_out_2;

  Clock clock_1 (.out(clock_1_out));
  Controle_de_Borda controle_de_borda_1 (.in_1(clock_1_out), .out_2(controle_de_borda_1_out_2));
  \Contador_Síncrono_Módulo_16__EN_OUT__CLK__EN_CLK__LOAD__CLR  \contador_síncrono_módulo_16_en_out_clk_en_clk_load_clr_1  (
    .EN_OUT(in_1), .EN_CLK(in_2), .LOAD(in_3), .CLR(in_4), .Q0(out_12), .Q1(out_11), .Q2(out_10), .Q3(out_9),
    .D0(in_8), .D1(in_7), .D2(in_6), .D3(in_5), .CLK(controle_de_borda_1_out_2));
endmodule

module Q06 (
  input  EN_OUT,
  input  LOAD,
  input  I7,
  input  I6,
  input  I5,
  input  I4,
  input  I3,
  input  I2,
  input  I1,
  input  I0,
  output O7,
  output O6,
  output O5,
  output O4,
  output O3,
  output O2,
  output O1,
  output O0
);

  Registrador_8_bits__EN_OUT__LOAD registrador_8_bits_en_out_load_1 (
    .EN_OUT(EN_OUT), .LOAD(LOAD), .O7(O7), .O6(O6), .O5(O5), .O4(O4), .O3(O3), .O2(O2), .O1(O1), .O0(O0),
    .I7(I7), .I6(I6), .I5(I5), .I4(I4), .I3(I3), .I2(I2), .I1(I1), .I0(I0));
endmodule

module Q07 (
  input  in_1,
  output out_2,
  output out_3,
  output out_4
);

  wire clock_1_out, controle_de_borda_1_out_2, not_1_out;

  Clock clock_1 (.out(clock_1_out));
  Controle_de_Borda controle_de_borda_1 (.in_1(clock_1_out), .out_2(controle_de_borda_1_out_2));
  not not_1 (not_1_out, controle_de_borda_1_out_2);
  \Contador_Síncrono_Módulo_8__Sequência_Personalizada  \contador_síncrono_módulo_8_sequência_personalizada_1  (
    .CLK(not_1_out), .\Início (in_1), .Q0(out_4), .Q1(out_3), .Q3(out_2));
endmodule

module Q08 (
  input  in_1,
  output Q5,
  output Q4,
  output Q3,
  output Q2,
  output Q1,
  output Q0
);

  wire clock_1_out, controle_de_borda_1_out_2, not_1_out;

  Clock clock_1 (.out(clock_1_out));
  Controle_de_Borda controle_de_borda_1 (.in_1(clock_1_out), .out_2(controle_de_borda_1_out_2));
  Contador_em_Anel contador_em_anel_1 (
    .START(in_1), .Q0(Q0), .Q1(Q1), .Q2(Q2), .Q3(Q3), .Q4(Q4), .Q5(Q5), .CLK(not_1_out));
  not not_1 (not_1_out, controle_de_borda_1_out_2);
endmodule

module Q09 (
  input  CLR,
  output Y3,
  output Y2,
  output Y1,
  output Y0
);

  wire clock_1_out, controle_de_borda_1_out_2;

  Clock clock_1 (.out(clock_1_out));
  Controle_de_Borda controle_de_borda_1 (.in_1(clock_1_out), .out_2(controle_de_borda_1_out_2));
  \Máquina_de_Estados_Finitos_1  \máquina_de_estados_finitos_1_1  (
    .CLR(CLR), .Y3(Y3), .Y2(Y2), .Y1(Y1), .Y0(Y0), .CLK(controle_de_borda_1_out_2));
endmodule

module Q10 (
  input  A,
  input  CLR,
  output Y3,
  output Y2,
  output Y1,
  output Y0
);

  wire clock_1_out, controle_de_borda_1_out_2;

  Clock clock_1 (.out(clock_1_out));
  Controle_de_Borda controle_de_borda_1 (.in_1(clock_1_out), .out_2(controle_de_borda_1_out_2));
  \Máquina_de_Estados_Finitos_2__Q10  \máquina_de_estados_finitos_2_q10_1  (
    .A(A), .CLK(controle_de_borda_1_out_2), .CLR(CLR), .Y3(Y3), .Y2(Y2), .Y1(Y1), .Y0(Y0));
endmodule
