// Logisim project Multiplexadores-Demultiplexadores.circ as structural Verilog: 9 circuits, main circuit main
module main (
  input  Input_15,
  input  Input_14,
  input  Input_13,
  input  Input_12,
  input  Input_11,
  input  Input_10,
  input  Input_9,
  input  Input_8,
  input  Input_7,
  input  Input_6,
  input  Input_5,
  input  Input_4,
  input  Input_3,
  input  Input_2,
  input  Input_1,
  input  Input_0,
  input  Select_3,
  input  Select_2,
  input  Select_1,
  input  Select_0,
  input  Select_3_2,
  input  Select_2_2,
  input  Select_1_2,
  input  Select_0_2,
  output Output_15,
  output Output_14,
  output Output_13,
  output Output_12,
  output Output_11,
  output Output_10,
  output Output_9,
  output Output_8,
  output Output_7,
  output Output_6,
  output Output_5,
  output Output_4,
  output Output_3,
  output Output_2,
  output Output_1,
  output Output_0
);

  wire mux_16x1_1_output;

  MUX_16x1 mux_16x1_1 (
    .Input_15(Input_15), .Input_14(Input_14), .Input_13(Input_13), .Input_12(Input_12), .Input_11(Input_11),
    .Input_10(Input_10), .Input_9(Input_9), .Input_8(Input_8), .Input_7(Input_7), .Input_6(Input_6),
    .Input_5(Input_5), .Input_4(Input_4), .Input_3(Input_3), .Input_2(Input_2), .Input_1(Input_1),
    .Input_0(Input_0), .Output(mux_16x1_1_output), .Select_3(Select_3), .Select_2(Select_2),
    .Select_1(Select_1), .Select_0(Select_0));
  DEMUX_1x16 demux_1x16_1 (
    .Input(mux_16x1_1_output), .Output_15(Output_15), .Output_14(Output_14), .Output_13(Output_13),
    .Output_12(Output_12), .Output_11(Output_11), .Output_10(Output_10), .Output_9(Output_9),
    .Output_8(Output_8), .Output_7(Output_7), .Output_6(Output_6), .Output_5(Output_5), .Output_4(Output_4),
    .Output_3(Output_3), .Output_2(Output_2), .Output_1(Output_1), .Output_0(Output_0),
    .Select_3(Select_3_2), .Select_2(Select_2_2), .Select_1(Select_1_2), .Select_0(Select_0_2));
endmodule

module MUX_2x1 (
  input  Input_1,
  input  Input_0,
  input  Select_0,
  output Output
);

  wire and_1_out, and_2_out, not_1_out;

  not not_1 (not_1_out, Select_0);
  and and_1 (and_1_out, Input_1, Select_0);
  and and_2 (and_2_out, Input_0, not_1_out);
  or or_1 (Output, and_1_out, and_2_out);
endmodule

module MUX_4x1 (
  input  Input_3,
  input  Input_2,
  input  Input_1,
  input  Input_0,
  input  Select_1,
  input  Select_0,
  output Output
);

  wire and_1_out, and_2_out, and_3_out, and_4_out, not_1_out, not_2_out, not_3_out, not_4_out;

  not not_1 (not_1_out, Select_0);
  not not_2 (not_2_out, Select_1);
  not not_3 (not_3_out, Select_1);
  not not_4 (not_4_out, Select_0);
  and and_1 (and_1_out, Input_3, Select_1, Select_0);
  and and_2 (and_2_out, Input_2, Select_1, not_1_out);
  and and_3 (and_3_out, Input_1, not_2_out, Select_0);
  and and_4 (and_4_out, Input_0, not_3_out, not_4_out);
  or or_1 (Output, and_1_out, and_2_out, and_3_out, and_4_out);
endmodule

module MUX_8x1 (
  input  Input_7,
  input  Input_6,
  input  Input_5,
  input  Input_4,
  input  Input_3,
  input  Input_2,
  input  Input_1,
  input  Input_0,
  input  Select_3,
  input  Select_1,
  input  Select_0,
  output Output
);

  wire mux_4x1_1_output, mux_4x1_2_output;

  MUX_4x1 mux_4x1_1 (
    .Input_3(Input_7), .Input_2(Input_6), .Input_1(Input_5), .Input_0(Input_4), .Output(mux_4x1_1_output),
    .Select_1(Select_1), .Select_0(Select_0));
  MUX_4x1 mux_4x1_2 (
    .Input_3(Input_3), .Input_2(Input_2), .Input_1(Input_1), .Input_0(Input_0), .Output(mux_4x1_2_output),
    .Select_1(Select_1), .Select_0(Select_0));
  MUX_2x1 mux_2x1_1 (.Input_1(mux_4x1_1_output), .Input_0(mux_4x1_2_output), .Output(Output), .Select_0(Select_3));
endmodule

module DEMUX_1x2 (
  input  Input,
  input  Select,
  output Output_1,
  output Output_0
);

  wire not_1_out;

  not not_1 (not_1_out, Select);
  and and_1 (Output_1, Input, Select);
  and and_2 (Output_0, Input, not_1_out);
endmodule

module DEMUX_1x4 (
  input  Input,
  input  Select_1,
  input  Select_0,
  output Output_3,
  output Output_2,
  output Output_1,
  output Output_0
);

  wire not_1_out, not_2_out, not_3_out, not_4_out;

  not not_1 (not_1_out, Select_0);
  not not_2 (not_2_out, Select_1);
  not not_3 (not_3_out, Select_1);
  not not_4 (not_4_out, Select_0);
  and and_1 (Output_3, Input, Select_1, Select_0);
  and and_2 (Output_2, Input, Select_1, not_1_out);
  and and_3 (Output_1, Input, not_2_out, Select_0);
  and and_4 (Output_0, Input, not_3_out, not_4_out);
endmodule

module DEMUX_1x8 (
  input  Input,
  input  Select_2,
  input  Select_1,
  input  Select_0,
  output Output_7,
  output Output_6,
  output Output_5,
  output Output_4,
  output Output_3,
  output Output_2,
  output Output_1,
  output Output_0
);

  wire demux_1x2_1_output_0, demux_1x2_1_output_1;

  DEMUX_1x2 demux_1x2_1 (
    .Input(Input), .Output_1(demux_1x2_1_output_1), .Output_0(demux_1x2_1_output_0), .Select(Select_2));
  DEMUX_1x4 demux_1x4_1 (
    .Input(demux_1x2_1_output_1), .Output_3(Output_7), .Output_2(Output_6), .Output_1(Output_5),
    .Output_0(Output_4), .Select_1(Select_1), .Select_0(Select_0));
  DEMUX_1x4 demux_1x4_2 (
    .Input(demux_1x2_1_output_0), .Output_3(Output_3), .Output_2(Output_2), .Output_1(Output_1),
    .Output_0(Output_0), .Select_1(Select_1), .Select_0(Select_0));
endmodule

module MUX_16x1 (
  input  Input_15,
  input  Input_14,
  input  Input_13,
  input  Input_12,
  input  Input_11,
  input  Input_10,
  input  Input_9,
  input  Input_8,
  input  Input_7,
  input  Input_6,
  input  Input_5,
  input  Input_4,
  input  Input_3,
  input  Input_2,
  input  Input_1,
  input  Input_0,
  input  Select_3,
  input  Select_2,
  input  Select_1,
  input  Select_0,
  output Output
);

  wire mux_4x1_1_output, mux_4x1_2_output, mux_4x1_3_output, mux_4x1_4_output;

  MUX_4x1 mux_4x1_1 (
    .Input_3(Input_15), .Input_2(Input_14), .Input_1(Input_13), .Input_0(Input_12),
    .Output(mux_4x1_1_output), .Select_1(Select_1), .Select_0(Select_0));
  MUX_4x1 mux_4x1_2 (
    .Input_3(Input_11), .Input_2(Input_10), .Input_1(Input_9), .Input_0(Input_8), .Output(mux_4x1_2_output),
    .Select_1(Select_1), .Select_0(Select_1));
  MUX_4x1 mux_4x1_3 (
    .Input_3(Input_7), .Input_2(Input_6), .Input_1(Input_5), .Input_0(Input_4), .Output(mux_4x1_3_output),
    .Select_1(Select_1), .Select_0(Select_0));
  MUX_4x1 mux_4x1_4 (
    .Input_3(Input_3), .Input_2(Input_2), .Input_1(Input_1), .Input_0(Input_0), .Output(mux_4x1_4_output),
    .Select_1(Select_1), .Select_0(Select_0));
  MUX_4x1 mux_4x1_5 (
    .Input_3(mux_4x1_1_output), .Input_2(mux_4x1_2_output), .Input_1(mux_4x1_3_output),
    .Input_0(mux_4x1_4_output), .Output(Output), .Select_1(Select_3), .Select_0(Select_2));
endmodule

module DEMUX_1x16 (
  input  Input,
  input  Select_3,
  input  Select_2,
  input  Select_1,
  input  Select_0,
  output Output_15,
  output Output_14,
  output Output_13,
  output Output_12,
  output Output_11,
  output Output_10,
  output Output_9,
  output Output_8,
  output Output_7,
  output Output_6,
  output Output_5,
  output Output_4,
  output Output_3,
  output Output_2,
  output Output_1,
  output Output_0
);

  wire demux_1x4_1_output_0, demux_1x4_1_output_1, demux_1x4_1_output_2, demux_1x4_1_output_3;

  DEMUX_1x4 demux_1x4_1 (
    .Input(Input), .Output_3(demux_1x4_1_output_3), .Output_2(demux_1x4_1_output_2),
    .Output_1(demux_1x4_1_output_1), .Output_0(demux_1x4_1_output_0), .Select_1(Select_3), .Select_0(Select_2));
  DEMUX_1x4 demux_1x4_2 (
    .Input(demux_1x4_1_output_3), .Output_3(Output_15), .Output_2(Output_14), .Output_1(Output_13),
    .Output_0(Output_12), .Select_1(Select_1), .Select_0(Select_0));
  DEMUX_1x4 demux_1x4_3 (
    .Input(demux_1x4_1_output_2), .Output_3(Output_11), .Output_2(Output_10), .Output_1(Output_9),
    .Output_0(Output_8), .Select_1(Select_1), .Select_0(Select_0));
  DEMUX_1x4 demux_1x4_4 (
    .Input(demux_1x4_1_output_1), .Output_3(Output_7), .Output_2(Output_6), .Output_1(Output_5),
    .Output_0(Output_4), .Select_1(Select_1), .Select_0(Select_0));
  DEMUX_1x4 demux_1x4_5 (
    .Input(demux_1x4_1_output_0), .Output_3(Output_3), .Output_2(Output_2), .Output_1(Output_1),
    .Output_0(Output_0), .Select_1(Select_1), .Select_0(Select_0));
endmodule
