// Logisim project Somador-Subtrator.circ as structural Verilog
module Somador_4bits (
  input  A3,
  input  A2,
  input  A1,
  input  A0,
  input  B3,
  input  B2,
  input  B1,
  input  B0,
  input  Ci,
  output Co,
  output S3,
  output S2,
  output S1,
  output S0
);

  wire somador_1bit_2_co, somador_1bit_3_co, somador_1bit_4_co;

  Somador_1bit somador_1bit_1 (.Ci(A3), .A(B3), .B(somador_1bit_3_co), .Co(Co), .S(S3));
  Somador_1bit somador_1bit_2 (.Ci(A1), .A(B1), .B(somador_1bit_4_co), .Co(somador_1bit_2_co), .S(S1));
  Somador_1bit somador_1bit_3 (.Ci(A2), .A(B2), .B(somador_1bit_2_co), .Co(somador_1bit_3_co), .S(S2));
  Somador_1bit somador_1bit_4 (.Ci(A0), .A(B0), .B(Ci), .Co(somador_1bit_4_co), .S(S0));
endmodule

module Somador_1bit (
  input  A,
  input  B,
  input  Ci,
  output Co,
  output S
);

  wire and_1_out, and_2_out, xor_1_out;

  and and_1 (and_1_out, B, A);
  and and_2 (and_2_out, Ci, xor_1_out);
  xor xor_1 (xor_1_out, B, A);
  or or_1 (Co, and_1_out, and_2_out);
  xor xor_2 (S, xor_1_out, Ci);
endmodule

module Somador_8bits (
  input  A7,
  input  A6,
  input  A5,
  input  A4,
  input  B7,
  input  B6,
  input  B5,
  input  B4,
  input  A3,
  input  A2,
  input  A1,
  input  A0,
  input  B3,
  input  B2,
  input  B1,
  input  B0,
  output Co,
  output S7,
  output S6,
  output S5,
  output S4,
  output S3,
  output S2,
  output S1,
  output S0
);

  wire somador_4bits_2_co;

  Somador_4bits somador_4bits_1 (
    .A3(A7), .A2(A6), .A1(A5), .A0(A4), .B3(B7), .B2(B6), .B1(B5), .B0(B4), .Co(Co), .S3(S6), .S2(S7),
    .S1(S5), .S0(S4), .Ci(somador_4bits_2_co));
  Somador_4bits somador_4bits_2 (
    .A3(A3), .A2(A2), .A1(A1), .A0(A0), .B3(B3), .B2(B2), .B1(B1), .B0(B0), .Co(somador_4bits_2_co), .S3(S2),
    .S2(S3), .S1(S1), .S0(S0), .Ci(1'b0));
endmodule
