// Logisim project SAP1_Timer.circ as structural Verilog: 24 circuits, main circuit main
module main (
  input  Reset,
  output [3:0] Dados,
  output [3:0] \Dados___Endereços ,
  output out_4,
  output out_5,
  output out_6,
  output out_7,
  output out_8,
  output out_9,
  output out_10,
  output out_11
);

  wire CLK, CLK_T, controlador_sequencializador_rom_1_hlt, Cp, Dec, Ea, Ec, Ep, Er, Et, Eu, Inc, Lp, Mul,
       nCE, nEi, nLa, nLb, nLc, nLi, nLm, nLo, nLr, nLt, not_1_out, not_2_out, not_3_out, not_4_out,
       \registrador_instruções_1_i4 , \registrador_instruções_1_i5 , \registrador_instruções_1_i6 ,
       \registrador_instruções_1_i7 , REP, Rep_Timer, Start_End, Su, TIMER, undriven, XX;
  wire [3:0] rem_1_remout;
  wire [7:0] acumulador_1_a_out_ula, countclocks_1_out_5, counter_1_q, cRep, cTimer,
       registrador_b_1_b_dataout, registrador_c_1_c_out;

  Clock Clock (.out(CLK_T));
  assign CLK = not_1_out ? CLK_T : 1'bz;  // Controlled_Buffer controlled_buffer_1
  not not_1 (not_1_out, controlador_sequencializador_rom_1_hlt);
  not not_2 (not_2_out, CLK);
  not not_3 (not_3_out, Reset);
  not not_4 (not_4_out, nCE);
  \Registrador_Instruções  \registrador_instruções_1  (
    .in_1({Dados, \Dados___Endereços }), .nLi(nLi), .CLK(CLK), .CLR(Reset), .nEi(nEi),
    .out_6(\Dados___Endereços ), .I4(\registrador_instruções_1_i4 ), .I5(\registrador_instruções_1_i5 ),
    .I6(\registrador_instruções_1_i6 ), .I7(\registrador_instruções_1_i7 ));
  Controlador_Sequencializador_ROM controlador_sequencializador_rom_1 (
    .CLK(CLK), .CLR(Reset), .HLT(controlador_sequencializador_rom_1_hlt), .Cp(Cp), .Ep(Ep), .nLm(nLm),
    .nCE(nCE), .nLl(nLi), .nEl(nEi), .nLa(nLa), .Ea(Ea), .Su(Su), .Eu(Eu), .nLb(nLb), .nLo(nLo),
    .I7(\registrador_instruções_1_i7 ), .I6(\registrador_instruções_1_i6 ),
    .I4(\registrador_instruções_1_i4 ), .Inc(Inc), .Dec(Dec), .Mul(Mul), .Lp(Lp),
    .I5(\registrador_instruções_1_i5 ), .Et(Et), .Er(Er), .nLt(nLt), .Ec(Ec), .Start_End(Start_End),
    .nLc(nLc), .nLr(nLr), .XX(XX), .XX_2(XX));
  Contador_Programa contador_programa_1 (
    .Lp(Lp), .Cp_In(\Dados___Endereços ), .Cp_Out(\Dados___Endereços ), .Cp(Cp), .nCLK(not_2_out),
    .nCLR(not_3_out), .Ep(Ep));
  REM rem_1 (.in_1(\Dados___Endereços ), .nLm(nLm), .CLK(CLK), .REMOut(rem_1_remout));
  \Memória_RAM  \memória_ram_1  (.in_1(rem_1_remout), .nCE(not_4_out), .CLK(CLK), .out_4({Dados, \Dados___Endereços }));
  ControladorTimer controladortimer_1 (
    .nLr(nLr), .REP(REP), .CLK(CLK_T), .TIMER(TIMER), .Start_End(Start_End), .Rep_Timer(Rep_Timer),
    .CLR(Reset));
  Timer timer_1 (
    .Input({Dados, \Dados___Endereços }), .CLK(CLK_T), .Et(Et), .Timer(TIMER), .Lt(nLt), .CLR(Reset),
    .Start_End(Start_End), .Rep_Timer(Rep_Timer), .InputC(registrador_c_1_c_out), .out_9(cTimer));
  Repetidor repetidor_1 (
    .Lr(nLr), .Input({Dados, \Dados___Endereços }), .CLK_T(CLK_T), .Er(Er), .Timer(REP),
    .Start_End(Start_End), .Rep_Timer(Rep_Timer), .CLR(Reset), .out_8(cRep));
  Acumulador acumulador_1 (
    .A_In({Dados, \Dados___Endereços }), .nLa(nLa), .CLK(CLK), .Ea(Ea), .A_Out_ULA(acumulador_1_a_out_ula),
    .A_Out({Dados, \Dados___Endereços }));
  Somador_Subtrator somador_subtrator_1 (
    .Su(Su), .B_data(registrador_b_1_b_dataout), .A_dataOut2({Dados, \Dados___Endereços }),
    .A_data(acumulador_1_a_out_ula), .Eu(Eu), .inc(Inc), .dec(Dec), .mul(Mul));
  Registrador_B registrador_b_1 (
    .B_dataIn({Dados, \Dados___Endereços }), .B_dataOut(registrador_b_1_b_dataout), .nLb(nLb), .CLK(CLK));
  Registrador_C registrador_c_1 (
    .C_In({Dados, \Dados___Endereços }), .nLc(nLc), .CLK(CLK), .Ec(Ec), .C_Out(registrador_c_1_c_out),
    .Start_End(Start_End), .Rep_Timer(Rep_Timer));
  \Indicação_Visual  \indicação_visual_1  (
    .Input({Dados, \Dados___Endereços }),
    .Output({out_4, out_5, out_6, out_7, out_8, out_9, out_10, out_11}), .nLo(nLo), .CLK(CLK), .CLR(Reset));
  Hex_Digit_Display hex_digit_display_1 (.value({out_4, out_5, out_6, out_7}));  // open: dp
  Hex_Digit_Display hex_digit_display_2 (.value({out_8, out_9, out_10, out_11}));  // open: dp
  DotMatrix #(.matrixcols(8), .matrixrows(1), .dotshape("circle")) dotmatrix_1 (
    .col0(out_4), .col1(out_5), .col2(out_6), .col3(out_7), .col4(out_8), .col5(out_9), .col6(out_10),
    .col7(out_11));
  Hex_Digit_Display hex_digit_display_3 (.value(counter_1_q[7:4]), .dp(undriven));
  Counter counter_1 (.Q(counter_1_q), .clk(CLK), .clr(Reset));  // open: load, D, count, carry
  Hex_Digit_Display hex_digit_display_4 (.value(cTimer[7:4]));  // open: dp
  Hex_Digit_Display hex_digit_display_5 (.value(counter_1_q[3:0]));  // open: dp
  Hex_Digit_Display hex_digit_display_6 (.value(cTimer[3:0]));  // open: dp
  Hex_Digit_Display hex_digit_display_7 (.value(countclocks_1_out_5[7:4]));  // open: dp
  CountClocks countclocks_1 (.out_5(countclocks_1_out_5), .CLK_T(CLK_T), .CLR(Reset), .in_3(Start_End), .in_4(REP));
  Hex_Digit_Display hex_digit_display_8 (.value(countclocks_1_out_5[3:0]));  // open: dp
  Hex_Digit_Display hex_digit_display_9 (.value(cRep[7:4]));  // open: dp
  Hex_Digit_Display hex_digit_display_10 (.value(cRep[3:0]));  // open: dp

  // Other names for the same wires on the sheet: CLR = Reset

  // Notes on the sheet:
  //   SAP-1 EM LOGISIM TIMER Ver2/2024
  //   Arquitetura de Computadores I
  //   Grupo:
  //   Instruções:
  //   LDA 0000: A<-*(MEM)
  //   ADD 0001: A<-A+B
  //   SUB 0010: A<-A-B
  //   INC 0011: A<=A+1
  //   DEC 0100: A<=A-1
  //   MUL 0101: A<-AxB
  //   JMP 0110: CP<-endereço de salto
  //   TMP 0111:  XXH para sistema por XX clocks
  //   OUT 1110: exibir o valor
  //   HLT 1111: interromper o circuito
  //   Como usar:
  //   Adicione as operações no bloco de memória RAM,
  //   execute um RESET e envie pulsos de clock.
  //   Esse trabalho foi uma modificação do trabalho feito por:
  //   As modificações foram feitas no controlador sequencializador.
  //   Com as alterações agora o controlador é implementado usando
  //   ROMs e possui ciclo variavél de máquina.
  //   - André Luís Silva de Paula
  //   - André Santos Alves
  //   - Nathan de Araújo Cunha Lisboa
  //   - Pedro Malta Boscatti
  //   - Sophia Damasceno Satuf
  //   Contador de clocks do timer
endmodule

module Contador_Programa (
  input  Lp,
  input  [3:0] Cp_In,
  input  Cp,
  input  nCLK,
  input  nCLR,
  input  Ep,
  output [3:0] Cp_Out
);

  wire not_1_out;
  wire [3:0] counter_1_q;

  not not_1 (not_1_out, nCLR);
  assign Cp_Out = Ep ? counter_1_q : 4'bz;  // Controlled_Buffer controlled_buffer_1
  Counter #(.width(4), .max('hf), .trigger("falling")) counter_1 (
    .load(Lp), .D(Cp_In), .count(Cp), .Q(counter_1_q), .clk(nCLK), .clr(not_1_out));  // open: carry
endmodule

module REM (
  input  [3:0] in_1,
  input  nLm,
  input  CLK,
  output [3:0] REMOut
);

  wire not_1_out;

  not not_1 (not_1_out, nLm);
  Register #(.width(4)) register_1 (.D(in_1), .en(not_1_out), .Q(REMOut), .clk(CLK));  // open: clr
endmodule

module \Memória_RAM  (
  input  [3:0] in_1,
  input  nCE,
  input  CLK,
  output [7:0] out_4
);

  RAM #(.addrWidth(4)) ram_1 (.addr(in_1), .data(out_4), .sel(nCE), .clk(CLK), .ld(nCE));  // open: clr

  // Notes on the sheet:
  //   Operações:
  //   Exemplo 1:  02 + 03 - 04 + 02 = 03
  //   0f e0 1e e0 2d e0 1f e0 f0 00 00 00 00 04 03 02
  //   Exemplo 2:  150 + 70 - 50 + 100 = ? 270
  //   0f e0 1e e0 2d e0 1c e0 f0 00 00 00 64 32 46 96
  //   Exemplo 3:  5 x 2 - 1 - 2 + 1 = 8
  //   0f e0 5e e0 40 e0 2e e0 30 e0 f0 00 00 00 02 05
  //   Exemplo 4:  Carrega A=1,Exibe A, Inc A, Exibe A, JMP para Inc A 
  //   0f e0 30 e0 62 f0
  //   Exemplo 5: 05 + 02 espera 08 clocks e mostra
  //   0f e0 1e 7d e0 f0 00 00 00 00 00 00 00 08 02 05
endmodule

module \Registrador_Instruções  (
  input  [7:0] in_1,
  input  nLi,
  input  CLK,
  input  CLR,
  input  nEi,
  output [3:0] out_6,
  output I4,
  output I5,
  output I6,
  output I7
);

  wire not_1_out, not_2_out;
  wire [3:0] register_1_q;

  not not_1 (not_1_out, nLi);
  not not_2 (not_2_out, nEi);
  Register register_1 (.D(in_1), .en(not_1_out), .Q({I7, I6, I5, I4, register_1_q}), .clk(CLK), .clr(CLR));
  assign out_6 = not_2_out ? register_1_q : 4'bz;  // Controlled_Buffer controlled_buffer_1
endmodule

module Acumulador (
  input  [7:0] A_In,
  input  nLa,
  input  CLK,
  input  Ea,
  output [7:0] A_Out_ULA,
  output [7:0] A_Out
);

  wire not_1_out;

  not not_1 (not_1_out, nLa);
  Register register_1 (.D(A_In), .en(not_1_out), .Q(A_Out_ULA), .clk(CLK));  // open: clr
  assign A_Out = Ea ? A_Out_ULA : 8'bz;  // Controlled_Buffer controlled_buffer_1
endmodule

module Somador_Subtrator (
  input  Su,
  input  inc,
  input  dec,
  input  [7:0] B_data,
  input  [7:0] A_data,
  input  Eu,
  input  mul,
  output [7:0] A_dataOut2
);

  wire not_1_out, or_1_out;
  wire [7:0] adder_1_out, controlled_buffer_1_out, multiplier_1_out, xor_1_out;

  or or_1 (or_1_out, inc, dec);
  not not_1 (not_1_out, or_1_out);
  assign controlled_buffer_1_out = or_1_out ? 8'h1 : 8'bz;  // Controlled_Buffer controlled_buffer_1
  assign controlled_buffer_1_out = not_1_out ? B_data : 8'bz;  // Controlled_Buffer controlled_buffer_2
  assign xor_1_out = {8{Su}} ^ controlled_buffer_1_out;  // XOR_Gate xor_1, 8 bits wide
  Adder adder_1 (.a(xor_1_out), .b(A_data), .out(adder_1_out), .cin(Su));  // open: cout
  Multiplier multiplier_1 (.a(B_data), .b(A_data), .out(multiplier_1_out));  // open: cin, cout
  assign A_dataOut2 = Eu ? adder_1_out : 8'bz;  // Controlled_Buffer controlled_buffer_3
  assign A_dataOut2 = mul ? multiplier_1_out : 8'bz;  // Controlled_Buffer controlled_buffer_4
endmodule

module Registrador_B (
  input  [7:0] B_dataIn,
  input  nLb,
  input  CLK,
  output [7:0] B_dataOut
);

  wire not_1_out;

  Register register_1 (.D(B_dataIn), .en(not_1_out), .Q(B_dataOut), .clk(CLK));  // open: clr
  not not_1 (not_1_out, nLb);
endmodule

module Decodificador (
  input  l7,
  input  l6,
  input  l5,
  input  l4,
  output LDA,
  output ADD,
  output SUB,
  output OUT,
  output HLT
);

  wire and_1_out, and_2_out, and_3_out, and_4_out, and_5_out, not_1_out, not_2_out, not_3_out, not_4_out;

  not not_1 (not_1_out, l7);
  not not_2 (not_2_out, l6);
  not not_3 (not_3_out, l5);
  not not_4 (not_4_out, l4);
  buf buffer_1 (LDA, and_1_out);
  and and_1 (and_1_out, not_1_out, not_2_out, not_3_out, not_4_out);
  and and_2 (and_2_out, not_1_out, not_2_out, not_3_out, l4);
  buf buffer_2 (ADD, and_2_out);
  and and_3 (and_3_out, not_1_out, not_2_out, l5, not_4_out);
  buf buffer_3 (SUB, and_3_out);
  and and_4 (and_4_out, l7, l6, l5, not_4_out);
  buf buffer_4 (OUT, and_4_out);
  and and_5 (and_5_out, l7, l6, l5, l4);
  buf buffer_5 (HLT, and_5_out);
endmodule

module \Indicação_Visual  (
  input  [7:0] Input,
  input  nLo,
  input  CLK,
  input  CLR,
  output [7:0] Output
);

  wire not_1_out;

  not not_1 (not_1_out, nLo);
  Register register_1 (.D(Input), .en(not_1_out), .Q(Output), .clk(CLK), .clr(CLR));
endmodule

module Timer (
  input  Lt,
  input  [7:0] Input,
  input  [7:0] InputC,
  input  CLK,
  input  Et,
  input  Start_End,
  input  Rep_Timer,
  input  CLR,
  output [7:0] out_9,
  output Timer
);

  wire and_1_out, and_2_out, and_3_out, or_1_out, or_2_out, or_3_out;
  wire [7:0] controlled_buffer_1_out;

  assign controlled_buffer_1_out = and_1_out ? Input : 8'bz;  // Controlled_Buffer controlled_buffer_1
  assign controlled_buffer_1_out = and_2_out ? InputC : 8'bz;  // Controlled_Buffer controlled_buffer_2
  assign controlled_buffer_1_out = or_1_out ? 8'h1 : 8'bz;  // Controlled_Buffer controlled_buffer_3
  or or_1 (or_1_out, CLR, ~Start_End);  // OR_Gate
  and and_1 (and_1_out, ~Start_End, ~Rep_Timer);  // AND_Gate
  and and_2 (and_2_out, Rep_Timer, Start_End);
  or or_2 (or_2_out, ~Lt, Start_End);  // OR_Gate
  or or_3 (or_3_out, Et, and_3_out);
  and and_3 (and_3_out, Start_End, ~Rep_Timer);  // AND_Gate
  ContadorDecrescente contadordecrescente_1 (
    .Load(or_2_out), .Entrada(controlled_buffer_1_out), .Enable_Clock(or_3_out), .nCLK(CLK),
    .EnableOutput(1'b1), .Saida(out_9));  // open: CLR
  Hex_Digit_Display hex_digit_display_1 (.value(out_9[3:0]));  // open: dp
  Hex_Digit_Display hex_digit_display_2 (.value(out_9[7:4]));  // open: dp
  and and_4 (Timer, out_9[0], ~out_9[1], ~out_9[2], ~out_9[3], ~out_9[4], ~out_9[5], ~out_9[6], ~out_9[7]);  // AND_Gate
endmodule

module Controlador_Sequencializador_ROM (
  input  I7,
  input  I6,
  input  I5,
  input  I4,
  input  Start_End,
  input  CLK,
  input  CLR,
  output Cp,
  output Ep,
  output nLm,
  output nCE,
  output nLl,
  output nEl,
  output nLa,
  output Ea,
  output Su,
  output Eu,
  output nLb,
  output nLo,
  output Inc,
  output Dec,
  output Mul,
  output Lp,
  output Et,
  output nLt,
  output Ec,
  output Er,
  output nLc,
  output nLr,
  output XX,
  output XX_2,
  output HLT
);

  wire and_1_out, and_2_out, and_3_out, and_4_out, and_5_out, and_7_out, and_8_out, clr_t, load, nop,
       nor_1_out, not_1_out, not_2_out, or_2_out, shift_register_1_q0, shift_register_1_q1,
       shift_register_1_q3, shift_register_1_q4;
  wire [5:0] counter_1_q, rom_1_data;

  or or_1 (HLT, Start_End, and_1_out);
  and and_1 (and_1_out, I7, I6, I5, I4);
  ROM #(.addrWidth(4), .dataWidth(6)) rom_1 (.addr({I7, I6, I5, I4}), .data(rom_1_data));  // open: sel
  or or_2 (or_2_out, CLR, nop);
  or or_3 (clr_t, or_2_out, nor_1_out);
  not not_1 (not_1_out, load);
  not not_2 (not_2_out, CLK);
  Shift_Register #(.length(6)) shift_register_1 (
    .in(nor_1_out), .clk(CLK), .clr(or_2_out), .q0(shift_register_1_q0), .q1(shift_register_1_q1), .q2(load),
    .q3(shift_register_1_q3), .q4(shift_register_1_q4));  // open: shift, out, load, d0, d1, d2, d3, d4, d5, q5
  Counter #(.width(6), .max('h3f), .ongoal("continue")) counter_1 (
    .load(load), .D(rom_1_data), .count(not_1_out), .Q(counter_1_q), .clk(not_2_out), .clr(clr_t));  // open: carry
  nor nor_1 (nor_1_out, shift_register_1_q0, shift_register_1_q1, load, shift_register_1_q3, shift_register_1_q4);
  ROM #(.addrWidth(6), .dataWidth(24)) rom_2 (
    .addr(counter_1_q),
    .data({Cp, Ep, nLm, nCE, nLl, nEl, nLa, Ea, Su, Eu, nLb, nLo, Inc, Dec, Mul, Lp, Et, nLt, Ec, Er, nLc, nLr, XX, XX_2}));  // open: sel
  and and_2 (and_2_out, ~Cp, ~Ep, nLm, nCE);  // AND_Gate
  and and_3 (and_3_out, nLl, nEl, nLa, ~Ea);  // AND_Gate
  and and_4 (and_4_out, ~Su, ~Eu, nLb, nLo);  // AND_Gate
  and and_5 (and_5_out, ~Inc, ~Dec, ~Mul, ~Lp);  // AND_Gate
  and and_6 (nop, and_2_out, and_3_out, and_4_out, and_5_out, and_7_out, and_8_out);
  and and_7 (and_7_out, ~Et, nLt, ~Ec, ~Er);  // AND_Gate
  and and_8 (and_8_out, nLc, nLr, ~XX, ~XX_2);  // AND_Gate

  // Notes on the sheet:
  //   contents of rom_1 (hex, n*v repeats v):
  //   3 6 9 10 13 16 19 20 23 26 4*0 c
  //   NOP:  3e304c
  //   contents of rom_2 (hex, n*v repeats v):
  //   5e304c be304c 26304c 1a304c 2c304c 3e304c 1a304c 2e104c 3c704c 1a304c 2e104c 3cf04c 3f204c 3e304c
  //   3e304c 0 3c784c 3e304c 3e304c 3cf44c 3e304c 3e304c 1a304c 2e104c 3c324c 3a314c 3e304c 3e304c 4*0
  //   1a304c 2e300c 3e308c 1a304c 2e3048 3e3058 1a304c 2e3044 3e304c
endmodule

module Registrador_C (
  input  [7:0] C_In,
  input  nLc,
  input  CLK,
  input  Ec,
  input  Start_End,
  input  Rep_Timer,
  output [7:0] C_Out
);

  wire and_1_out, not_1_out, or_1_out;
  wire [7:0] register_1_q;

  not not_1 (not_1_out, nLc);
  and and_1 (and_1_out, Start_End, Rep_Timer);
  Register register_1 (.D(C_In), .en(not_1_out), .Q(register_1_q), .clk(CLK));  // open: clr
  or or_1 (or_1_out, Ec, and_1_out);
  assign C_Out = or_1_out ? register_1_q : 8'bz;  // Controlled_Buffer controlled_buffer_1
endmodule

module ContadorDecrescente (
  input  Load,
  input  [7:0] Entrada,
  input  Enable_Clock,
  input  nCLK,
  input  CLR,
  input  EnableOutput,
  output [7:0] Saida
);

  wire [7:0] counter_1_q;

  Counter counter_1 (
    .load(Load), .D(Entrada), .count(Enable_Clock), .Q(counter_1_q), .clk(nCLK), .clr(CLR));  // open: carry
  assign Saida = EnableOutput ? counter_1_q : 8'bz;  // Controlled_Buffer controlled_buffer_1
endmodule

module ContadorDecrescente2_seOutroNFor (
  input  Load,
  input  [7:0] Entrada,
  input  Enable_Clock,
  input  nCLK,
  input  nClear,
  input  EnableOutput,
  output [7:0] Saida
);

  wire counter_1_carry;
  wire [7:0] counter_1_q, not_1_out;

  Counter #(.trigger("falling")) counter_1 (
    .load(Load), .D(Entrada), .count(Enable_Clock), .Q(counter_1_q), .carry(counter_1_carry), .clk(nCLK),
    .clr(nClear));
  not not_1 (not_1_out[0], counter_1_q[0]);
  not not_2 (not_1_out[1], counter_1_q[1]);
  not not_3 (not_1_out[2], counter_1_q[2]);
  not not_4 (not_1_out[3], counter_1_q[3]);
  not not_5 (not_1_out[4], counter_1_q[4]);
  not not_6 (not_1_out[5], counter_1_q[5]);
  not not_7 (not_1_out[6], counter_1_q[6]);
  not not_8 (not_1_out[7], counter_1_q[7]);
  assign Saida = EnableOutput ? not_1_out : 8'bz;  // Controlled_Buffer controlled_buffer_1
endmodule

module CountClocks (
  input  CLK_T,
  input  CLR,
  input  in_3,
  input  in_4,
  output [7:0] out_5
);

  wire and_1_out, and_2_out, d_ff_1_q;

  and and_1 (and_1_out, in_3, ~in_4);  // AND_Gate
  D_Flip_Flop d_ff_1 (.clk(CLK_T), .D(and_1_out), .Q(d_ff_1_q));  // open: Qn, preset, en, reset
  Counter counter_1 (.Q(out_5), .clk(and_2_out), .clr(CLR));  // open: load, D, count, carry
  and and_2 (and_2_out, CLK_T, d_ff_1_q);
endmodule

module Repetidor (
  input  Lr,
  input  CLK_T,
  input  [7:0] Input,
  input  Start_End,
  input  Er,
  input  Rep_Timer,
  input  CLR,
  output [7:0] out_8,
  output Timer
);

  wire and_1_out, and_2_out, and_3_out, not_1_out, not_2_out, or_1_out, or_2_out;

  and and_1 (and_1_out, CLK_T, Start_End, Rep_Timer);
  and and_2 (and_2_out, CLK_T, ~Start_End);  // AND_Gate
  or or_1 (or_1_out, and_1_out, and_2_out);
  and and_3 (and_3_out, ~Start_End, Rep_Timer);  // AND_Gate
  not not_1 (not_1_out, Lr);
  not not_2 (not_2_out, Er);
  or or_2 (or_2_out, and_3_out, CLR);
  Hex_Digit_Display hex_digit_display_1 (.value(out_8[7:4]));  // open: dp
  ContadorDecrescente contadordecrescente_1 (
    .Load(not_1_out), .Entrada(Input), .Enable_Clock(not_2_out), .nCLK(or_1_out), .EnableOutput(1'b1),
    .Saida(out_8), .CLR(or_2_out));
  Hex_Digit_Display hex_digit_display_2 (.value(out_8[3:0]));  // open: dp
  nor nor_1 (Timer, out_8[0], out_8[1], out_8[2], out_8[3], out_8[4], out_8[5], out_8[6], out_8[7]);
endmodule

module ControladorTimer (
  input  nLr,
  input  REP,
  input  CLK,
  input  TIMER,
  input  CLR,
  output Start_End,
  output Rep_Timer
);

  wire and_1_out, and_2_out, and_3_out, and_4_out, not_1_out, or_1_out, or_2_out;

  and and_1 (and_1_out, ~Start_End, ~nLr);  // AND_Gate
  and and_2 (and_2_out, REP, TIMER);
  not not_1 (not_1_out, CLK);
  and and_3 (and_3_out, Start_End, TIMER);
  and and_4 (and_4_out, Start_End, ~TIMER);  // AND_Gate
  Latch_SR latch_sr_1 (.S(and_3_out), .R(or_1_out), .Q(Rep_Timer));  // open: Não_Q
  or or_1 (or_1_out, and_4_out, or_2_out);
  J_K_Flip_Flop j_k_ff_1 (
    .J(and_1_out), .clk(not_1_out), .K(and_2_out), .Q(Start_End), .preset(1'b0), .en(1'b1), .reset(or_2_out));  // open: Qn
  or or_2 (or_2_out, CLR, nLr);
endmodule

module Latch_SR (
  input  S,
  input  R,
  output \Não_Q ,
  output Q
);

  nor nor_1 (\Não_Q , S, Q);
  nor nor_2 (Q, \Não_Q , R);
endmodule

module Controle_de_Borda (
  input  in_1,
  output out_2
);

  wire and_1_out, not_1_out;

  and and_1 (and_1_out, not_1_out, not_1_out);
  not not_1 (not_1_out, in_1);
  and and_2 (out_2, in_1, and_1_out);
endmodule

module Flip_Flop_JK__PRE__CLR (
  input  Preset,
  input  J,
  input  CLK,
  input  K,
  input  Clear,
  output Q,
  output nQ
);

  wire and_1_out, and_2_out, controle_de_borda_1_out_2, nand_1_out, nand_2_out, not_1_out, not_2_out;

  and and_1 (and_1_out, nQ, J);
  Latches_FlipFlops_Controle_de_Borda controle_de_borda_1 (.in_1(CLK), .out_2(controle_de_borda_1_out_2));
  and and_2 (and_2_out, K, Q);
  not not_1 (not_1_out, Preset);
  nand nand_1 (nand_1_out, and_1_out, controle_de_borda_1_out_2);
  nand nand_2 (nand_2_out, controle_de_borda_1_out_2, and_2_out);
  not not_2 (not_2_out, Clear);
  nand nand_3 (Q, not_1_out, nand_1_out, nQ);
  nand nand_4 (nQ, Q, nand_2_out, not_2_out);
endmodule

module Flip_Flop_JK__PRE__CLR__sPRE__sCLR__EN_CLK (
  input  PRE,
  input  J,
  input  CLK,
  input  K,
  input  CLR,
  input  sPRE,
  input  sCLR,
  input  CLK_EN,
  output Q,
  output nQ
);

  wire and_1_out, and_2_out, and_3_out, and_4_out, or_1_out, or_2_out;

  or or_1 (or_1_out, J, sPRE);
  and and_1 (and_1_out, ~sPRE, K);  // AND_Gate
  and and_2 (and_2_out, or_1_out, ~sCLR);  // AND_Gate
  or or_2 (or_2_out, sCLR, and_1_out);
  and and_3 (and_3_out, and_2_out, CLK_EN);
  and and_4 (and_4_out, CLK_EN, or_2_out);
  Flip_Flop_JK__PRE_CLR ff_jk_pre_clr_1 (
    .J(and_3_out), .Q(Q), .nQ(nQ), .K(and_4_out), .Preset(PRE), .Clear(CLR), .CLK(CLK));
endmodule

module Flip_Flop_T__PRE__CLR__sPRE__sCLR__CLK_EN (
  input  sPRE,
  input  PRE,
  input  T,
  input  CLK,
  input  sCLR,
  input  EN,
  input  CLR,
  output Q,
  output nQ
);

  Flip_Flop_JK__PRE__CLR__sPRE__sCLR__CLK_EN ff_jk_pre_clr_spre_sclr_clk_en_1 (
    .J(T), .K(T), .Q(Q), .nQ(nQ), .PRE(PRE), .sPRE(sPRE), .sCLR(sCLR), .CLK_EN(EN), .CLR(CLR), .CLK(CLK));
endmodule

module \Contador_Síncrono_Módulo_256__EN_OUT__CLK__EN_CLK__LOAD__CLR  (
  input  EN_OUT,
  input  CLK,
  input  EN_CLK,
  input  LOAD,
  input  CLR1,
  input  CLR0,
  input  [7:0] in_7,
  output [7:0] out_8
);

  wire and_1_out, and_2_out, and_3_out, and_4_out, and_5_out, and_6_out, and_7_out, and_8_out, and_9_out,
       and_10_out, and_11_out, and_12_out, and_13_out, and_14_out, and_15_out, and_16_out, and_17_out,
       and_18_out, and_19_out, and_20_out, and_21_out, and_22_out, and_23_out,
       ff_t_pre_clr_spre_sclr_clk_en_1_q, ff_t_pre_clr_spre_sclr_clk_en_2_q,
       ff_t_pre_clr_spre_sclr_clk_en_3_q, ff_t_pre_clr_spre_sclr_clk_en_4_q,
       ff_t_pre_clr_spre_sclr_clk_en_5_q, ff_t_pre_clr_spre_sclr_clk_en_6_q,
       ff_t_pre_clr_spre_sclr_clk_en_7_q, ff_t_pre_clr_spre_sclr_clk_en_8_q, or_1_out, or_2_out, or_3_out,
       or_4_out, or_5_out, or_6_out, or_7_out;

  and and_1 (and_1_out, ~EN_CLK, LOAD);  // AND_Gate
  and and_2 (and_2_out, in_7[0], and_1_out);
  and and_3 (and_3_out, ~in_7[0], and_1_out);  // AND_Gate
  assign out_8[0] = EN_OUT ? ff_t_pre_clr_spre_sclr_clk_en_1_q : 1'bz;  // Controlled_Buffer controlled_buffer_1
  Latches_FlipFlops_Flip_Flop_T__PRE__CLR__sPRE__sCLR__CLK_EN ff_t_pre_clr_spre_sclr_clk_en_1 (
    .T(1'b1), .CLK(CLK), .Q(ff_t_pre_clr_spre_sclr_clk_en_1_q), .sPRE(and_2_out), .PRE(CLR1),
    .sCLR(and_3_out), .EN(1'b1), .CLR(CLR0));  // open: nQ
  and and_4 (and_4_out, in_7[1], and_1_out);
  and and_5 (and_5_out, ~in_7[1], and_1_out);  // AND_Gate
  assign out_8[1] = EN_OUT ? ff_t_pre_clr_spre_sclr_clk_en_2_q : 1'bz;  // Controlled_Buffer controlled_buffer_2
  Latches_FlipFlops_Flip_Flop_T__PRE__CLR__sPRE__sCLR__CLK_EN ff_t_pre_clr_spre_sclr_clk_en_2 (
    .T(ff_t_pre_clr_spre_sclr_clk_en_1_q), .CLK(CLK), .Q(ff_t_pre_clr_spre_sclr_clk_en_2_q),
    .sPRE(and_4_out), .PRE(1'b0), .sCLR(and_5_out), .EN(1'b1), .CLR(or_1_out));  // open: nQ
  or or_1 (or_1_out, CLR1, CLR0);
  and and_6 (and_6_out, in_7[2], and_1_out);
  and and_7 (and_7_out, ff_t_pre_clr_spre_sclr_clk_en_1_q, ff_t_pre_clr_spre_sclr_clk_en_2_q);
  and and_8 (and_8_out, ~in_7[2], and_1_out);  // AND_Gate
  assign out_8[2] = EN_OUT ? ff_t_pre_clr_spre_sclr_clk_en_3_q : 1'bz;  // Controlled_Buffer controlled_buffer_3
  Latches_FlipFlops_Flip_Flop_T__PRE__CLR__sPRE__sCLR__CLK_EN ff_t_pre_clr_spre_sclr_clk_en_3 (
    .T(and_7_out), .CLK(CLK), .Q(ff_t_pre_clr_spre_sclr_clk_en_3_q), .sPRE(and_6_out), .PRE(1'b0),
    .sCLR(and_8_out), .EN(1'b1), .CLR(or_2_out));  // open: nQ
  or or_2 (or_2_out, CLR1, CLR0);
  and and_9 (and_9_out, and_7_out, ff_t_pre_clr_spre_sclr_clk_en_3_q);
  assign out_8[3] = EN_OUT ? ff_t_pre_clr_spre_sclr_clk_en_4_q : 1'bz;  // Controlled_Buffer controlled_buffer_4
  and and_10 (and_10_out, in_7[3], and_1_out);
  Latches_FlipFlops_Flip_Flop_T__PRE__CLR__sPRE__sCLR__CLK_EN ff_t_pre_clr_spre_sclr_clk_en_4 (
    .T(and_9_out), .CLK(CLK), .Q(ff_t_pre_clr_spre_sclr_clk_en_4_q), .sPRE(and_10_out), .PRE(1'b0),
    .sCLR(and_11_out), .EN(1'b1), .CLR(or_3_out));  // open: nQ
  or or_3 (or_3_out, CLR1, CLR0);
  and and_11 (and_11_out, ~in_7[3], and_1_out);  // AND_Gate
  and and_12 (and_12_out, and_9_out, ff_t_pre_clr_spre_sclr_clk_en_4_q);
  and and_13 (and_13_out, in_7[4], and_1_out);
  Latches_FlipFlops_Flip_Flop_T__PRE__CLR__sPRE__sCLR__CLK_EN ff_t_pre_clr_spre_sclr_clk_en_5 (
    .T(and_12_out), .CLK(CLK), .Q(ff_t_pre_clr_spre_sclr_clk_en_5_q), .sPRE(and_13_out), .PRE(1'b0),
    .sCLR(and_14_out), .EN(1'b1), .CLR(or_4_out));  // open: nQ
  or or_4 (or_4_out, CLR1, CLR0);
  and and_14 (and_14_out, ~in_7[4], and_1_out);  // AND_Gate
  assign out_8[4] = EN_OUT ? ff_t_pre_clr_spre_sclr_clk_en_5_q : 1'bz;  // Controlled_Buffer controlled_buffer_5
  and and_15 (and_15_out, and_12_out, ff_t_pre_clr_spre_sclr_clk_en_5_q);
  and and_16 (and_16_out, in_7[5], and_1_out);
  and and_17 (and_17_out, ~in_7[5], and_1_out);  // AND_Gate
  assign out_8[5] = EN_OUT ? ff_t_pre_clr_spre_sclr_clk_en_6_q : 1'bz;  // Controlled_Buffer controlled_buffer_6
  Latches_FlipFlops_Flip_Flop_T__PRE__CLR__sPRE__sCLR__CLK_EN ff_t_pre_clr_spre_sclr_clk_en_6 (
    .T(and_15_out), .CLK(CLK), .Q(ff_t_pre_clr_spre_sclr_clk_en_6_q), .sPRE(and_16_out), .PRE(1'b0),
    .sCLR(and_17_out), .EN(1'b1), .CLR(or_5_out));  // open: nQ
  or or_5 (or_5_out, CLR1, CLR0);
  and and_18 (and_18_out, in_7[6], and_1_out);
  and and_19 (and_19_out, and_15_out, ff_t_pre_clr_spre_sclr_clk_en_6_q);
  and and_20 (and_20_out, ~in_7[6], and_1_out);  // AND_Gate
  assign out_8[6] = EN_OUT ? ff_t_pre_clr_spre_sclr_clk_en_7_q : 1'bz;  // Controlled_Buffer controlled_buffer_7
  Latches_FlipFlops_Flip_Flop_T__PRE__CLR__sPRE__sCLR__CLK_EN ff_t_pre_clr_spre_sclr_clk_en_7 (
    .T(and_19_out), .CLK(CLK), .Q(ff_t_pre_clr_spre_sclr_clk_en_7_q), .sPRE(and_18_out), .PRE(1'b0),
    .sCLR(and_20_out), .EN(1'b1), .CLR(or_6_out));  // open: nQ
  or or_6 (or_6_out, CLR1, CLR0);
  and and_21 (and_21_out, and_19_out, ff_t_pre_clr_spre_sclr_clk_en_7_q);
  assign out_8[7] = EN_OUT ? ff_t_pre_clr_spre_sclr_clk_en_8_q : 1'bz;  // Controlled_Buffer controlled_buffer_8
  and and_22 (and_22_out, in_7[7], and_1_out);
  Latches_FlipFlops_Flip_Flop_T__PRE__CLR__sPRE__sCLR__CLK_EN ff_t_pre_clr_spre_sclr_clk_en_8 (
    .T(and_21_out), .CLK(CLK), .Q(ff_t_pre_clr_spre_sclr_clk_en_8_q), .sPRE(and_22_out), .PRE(1'b0),
    .sCLR(and_23_out), .EN(1'b1), .CLR(or_7_out));  // open: nQ
  or or_7 (or_7_out, CLR1, CLR0);
  and and_23 (and_23_out, ~in_7[7], and_1_out);  // AND_Gate
endmodule
